// Logisim project automatic-car-solution.circ as structural Verilog: 1 circuit, main circuit main
module main (
  input  T,
  input  X,
  output [1:0] Displayed_State,
  output [1:0] Current_State
);

  wire and_1_out, and_2_out, and_3_out, and_4_out, clock_1_out, n0_out, n1_out;
  wire [1:0] or_2_out;

  Register #(.width(2)) register_1 (.D(or_2_out), .clk(clock_1_out), .Q(Current_State));  // open: en, clr
  Clock clock_1 (.out(clock_1_out));
  or or_1 (or_2_out[1], n1_out, and_1_out);
  and n1 (n1_out, ~Current_State[1], Current_State[0], T, ~X);  // AND_Gate
  and and_1 (and_1_out, Current_State[1], ~Current_State[0], T, ~X);  // AND_Gate
  Multiplexer #(.enable("true"), .select(2), .width(2)) multiplexer_1 (
    .in0(2'b11), .in1(2'b01), .in2(2'b00), .out(Displayed_State), .sel(Current_State));  // open: in3, en
  or or_2 (or_2_out[0], and_2_out, and_3_out, n0_out, and_4_out);
  and and_2 (and_2_out, ~Current_State[0], ~Current_State[1], ~T, ~X);  // AND_Gate
  and and_3 (and_3_out, ~Current_State[0], ~Current_State[1], T, ~X);  // AND_Gate
  and n0 (n0_out, ~Current_State[0], Current_State[1], ~T, ~X);  // AND_Gate
  and and_4 (and_4_out, Current_State[0], ~Current_State[1], ~T, ~X);  // AND_Gate
endmodule
