// Logisim project fsm-session6-solution.circ as structural Verilog: 1 circuit, main circuit main
module main (
  input  x,
  input  y,
  output F,
  output G,
  output H,
  output [1:0] out_6,
  output [1:0] out_7
);

  wire and_1_out, and_2_out, and_3_out, and_4_out, and_5_out, and_6_out, and_7_out, and_8_out, and_10_out,
       and_11_out, clock_1_out;

  Clock clock_1 (.out(clock_1_out));
  Register #(.width(2)) register_1 (.D(out_6), .clk(clock_1_out), .Q(out_7));  // open: en, clr
  or n1 (out_6[1], and_1_out, and_2_out, and_3_out, and_4_out);
  and and_1 (and_1_out, ~out_7[1], ~out_7[0], x, ~y);  // AND_Gate
  and and_2 (and_2_out, out_7[1], ~out_7[0], ~x, ~y);  // AND_Gate
  and and_3 (and_3_out, out_7[1], ~out_7[0], x, y);  // AND_Gate
  and and_4 (and_4_out, ~out_7[1], out_7[0], ~x, y);  // AND_Gate
  and and_5 (and_5_out, ~out_7[1], ~out_7[0], ~x, y);  // AND_Gate
  and and_6 (and_6_out, out_7[1], ~out_7[0], x, ~y);  // AND_Gate
  and and_7 (and_7_out, ~out_7[1], out_7[0], ~x, ~y);  // AND_Gate
  and and_8 (and_8_out, ~out_7[1], out_7[0], x, y);  // AND_Gate
  and and_9 (F, ~out_7[1], ~out_7[0]);  // AND_Gate
  and and_10 (and_10_out, ~out_7[1], ~out_7[0]);  // AND_Gate
  or or_1 (H, and_10_out, and_11_out);
  and and_11 (and_11_out, ~out_7[1], out_7[0]);  // AND_Gate
  or n0 (out_6[0], and_5_out, and_6_out, and_7_out, and_8_out);

  assign G = F;

  // Notes on the sheet:
  //   next state
  //   n1 = c1'c0'xy' + c1c0'x'y' + c1c0'xy + c1'c0x'y
  //   current state
  //   c1 c0 x y
  //   F = c1'c0'
  //   G = c1'c0'
  //   H = c1'c0' + c1'c0 
  //   n0 = c1'c0'x'y + c1c0'xy' + c1'c0x'y' + c1'c0xy
endmodule
