// Logisim project sheridan_a1.circ as structural Verilog: 2 circuits, main circuit main
module main (
  input  a0,
  input  a1,
  input  a2,
  input  a3,
  input  [1:0] b10,
  input  [1:0] b32,
  input  c0,
  input  [2:0] c321,
  input  [2:0] d
);

  wire mapping_1_dot0, mapping_1_dot1, mapping_1_dot2;
  wire [3:0] mapping_1_hex0, mapping_1_hex1, mapping_1_hex2;

  Mapping mapping_1 (
    .a0(a0), .a1(a1), .a2(a2), .a3(a3), .b10(b10), .b32(b32), .c0(c0), .c321(c321), .d(d),
    .hex0(mapping_1_hex0), .hex1(mapping_1_hex1), .hex2(mapping_1_hex2), .dot0(mapping_1_dot0),
    .dot1(mapping_1_dot1), .dot2(mapping_1_dot2));
  Hex_Digit_Display hex2 (.value(mapping_1_hex2));  // open: dp
  Hex_Digit_Display hex1 (.value(mapping_1_hex1));  // open: dp
  Hex_Digit_Display hex0 (.value(mapping_1_hex0));  // open: dp
endmodule

module Mapping (
  input  a0,
  input  a1,
  input  a2,
  input  a3,
  input  [1:0] b10,
  input  [1:0] b32,
  input  c0,
  input  [2:0] c321,
  input  [2:0] d,
  output [3:0] hex0,
  output [3:0] hex1,
  output [3:0] hex2,
  output dot0,
  output dot1,
  output dot2
);


  assign dot0 = d[2];
  assign dot1 = d[1];
  assign dot2 = d[0];
  assign hex0 = {a3, a2, a1, a0};
  assign hex1 = {b32, b10};
  assign hex2 = {c321, c0};
endmodule
