// Logisim project sheridan_a2.circ as structural Verilog
module CircuitRepresentation (
  input  o,
  input  p,
  input  q,
  input  r,
  output F,
  output G,
  output H
);

  wire and_1_out, and_2_out, and_3_out, and_4_out, and_5_out, and_6_out, and_7_out, and_8_out, and_9_out,
       and_10_out, and_11_out, and_12_out, and_14_out, and_15_out, not_1_out, not_2_out, not_3_out, not_4_out;

  not not_1 (not_1_out, o);
  not not_2 (not_2_out, p);
  not not_3 (not_3_out, q);
  not not_4 (not_4_out, r);
  and and_1 (and_1_out, not_1_out, not_2_out, not_3_out, not_4_out);
  and and_2 (and_2_out, not_1_out, not_2_out, q, r);
  and and_3 (and_3_out, not_1_out, p, not_3_out, not_4_out);
  and and_4 (and_4_out, not_1_out, p, q, r);
  and and_5 (and_5_out, not_1_out, not_2_out, not_3_out, r);
  and and_6 (and_6_out, o, not_2_out, q, not_4_out);
  and and_7 (and_7_out, o, p, not_3_out, r);
  and and_8 (and_8_out, o, p, q, r);
  and and_9 (and_9_out, not_1_out, p, q, not_4_out);
  and and_10 (and_10_out, o, not_2_out, not_3_out, not_4_out);
  and and_11 (and_11_out, o, not_2_out, not_3_out, r);
  and and_12 (and_12_out, o, not_2_out, q, r);
  // AND_Gate and_13 has open pins: in0=o, in1=p, in2=q, in3=not_4_out, out=open
  and and_14 (and_14_out, not_1_out, not_2_out, q, not_4_out);
  and and_15 (and_15_out, o, o, not_3_out, not_4_out);
  or or_1 (F, and_1_out, and_14_out, and_2_out, and_3_out, and_4_out, and_15_out);
  or or_2 (G, and_1_out, and_5_out, and_6_out, and_7_out, and_8_out);
  or or_3 (H, and_14_out, and_9_out, and_10_out, and_11_out, and_12_out);
endmodule
