// Logisim project sheridan_a3.circ as structural Verilog: 7 circuits, main circuit main
module main (
  input  [3:0] input_value,
  input  [2:0] demux_select,
  input  [2:0] mux_select
);

  wire [3:0] demuxfourbit_1_d0, demuxfourbit_1_d1, demuxfourbit_1_d2, demuxfourbit_1_d3, demuxfourbit_1_d4,
       demuxfourbit_1_d5, demuxfourbit_1_d6, demuxfourbit_1_d7, muxfourbit_1_m;

  Hex_Digit_Display hex_digit_display_1 (.value(demuxfourbit_1_d7));  // open: dp
  Hex_Digit_Display hex_digit_display_2 (.value(demuxfourbit_1_d6));  // open: dp
  Hex_Digit_Display hex_digit_display_3 (.value(demuxfourbit_1_d5));  // open: dp
  Hex_Digit_Display hex_digit_display_4 (.value(demuxfourbit_1_d4));  // open: dp
  DemuxFourBit demuxfourbit_1 (
    .i_demux(input_value), .select_demux(demux_select), .d7(demuxfourbit_1_d7), .d6(demuxfourbit_1_d6),
    .d5(demuxfourbit_1_d5), .d4(demuxfourbit_1_d4), .d3(demuxfourbit_1_d3), .d2(demuxfourbit_1_d2),
    .d1(demuxfourbit_1_d1), .d0(demuxfourbit_1_d0));
  Hex_Digit_Display hex_digit_display_5 (.value(demuxfourbit_1_d3));  // open: dp
  Hex_Digit_Display hex_digit_display_6 (.value(demuxfourbit_1_d2));  // open: dp
  Hex_Digit_Display hex_digit_display_7 (.value(demuxfourbit_1_d1));  // open: dp
  Hex_Digit_Display hex_digit_display_8 (.value(demuxfourbit_1_d0));  // open: dp
  Hex_Digit_Display hex_digit_display_9 (.value(muxfourbit_1_m));  // open: dp
  MuxFourBit muxfourbit_1 (
    .k7(demuxfourbit_1_d7), .k6(demuxfourbit_1_d6), .k5(demuxfourbit_1_d5), .k4(demuxfourbit_1_d4),
    .k3(demuxfourbit_1_d3), .k2(demuxfourbit_1_d2), .k1(demuxfourbit_1_d1), .k0(demuxfourbit_1_d0),
    .select_mux(mux_select), .m(muxfourbit_1_m));

  // Notes on the sheet:
  //   d7
  //   d6
  //   d5
  //   d4
  //   d3
  //   d2
  //   d1
  //   d0
  //   mux
endmodule

module DemuxOneBit (
  input  b,
  input  [2:0] s2s1s0,
  output G7,
  output G6,
  output G5,
  output G4,
  output G3,
  output G2,
  output G1,
  output G0
);

  wire s0_out, s1_out, s2_out;

  not s2 (s2_out, s2s1s0[2]);
  not s1 (s1_out, s2s1s0[1]);
  not s0 (s0_out, s2s1s0[0]);
  and seven (G7, b, s2s1s0[2], s2s1s0[1], s2s1s0[0]);
  and and_1 (G6, b, s2s1s0[2], s2s1s0[1], s0_out);
  and and_2 (G5, b, s2s1s0[2], s1_out, s2s1s0[0]);
  and and_3 (G4, b, s2s1s0[2], s1_out, s0_out);
  and and_4 (G3, b, s2_out, s2s1s0[1], s2s1s0[0]);
  and and_5 (G2, b, s2_out, s2s1s0[1], s0_out);
  and and_6 (G1, b, s2_out, s1_out, s2s1s0[0]);
  and zero (G0, b, s2_out, s1_out, s0_out);
endmodule

module DemuxTwoBit (
  input  [1:0] i_demux,
  input  [2:0] select_demux,
  output [1:0] d7,
  output [1:0] d6,
  output [1:0] d5,
  output [1:0] d4,
  output [1:0] d3,
  output [1:0] d2,
  output [1:0] d1,
  output [1:0] d0
);

  DemuxOneBit demuxonebit_1 (
    .b(i_demux[0]), .s2s1s0(select_demux), .G7(d7[0]), .G6(d6[0]), .G5(d5[0]), .G4(d4[0]), .G3(d3[0]),
    .G2(d2[0]), .G1(d1[0]), .G0(d0[0]));
  DemuxOneBit demuxonebit_2 (
    .b(i_demux[1]), .s2s1s0(select_demux), .G7(d7[1]), .G6(d6[1]), .G5(d5[1]), .G4(d4[1]), .G3(d3[1]),
    .G2(d2[1]), .G1(d1[1]), .G0(d0[1]));
endmodule

module DemuxFourBit (
  input  [3:0] i_demux,
  input  [2:0] select_demux,
  output [3:0] d7,
  output [3:0] d6,
  output [3:0] d5,
  output [3:0] d4,
  output [3:0] d3,
  output [3:0] d2,
  output [3:0] d1,
  output [3:0] d0
);

  DemuxTwoBit demuxtwobit_1 (
    .i_demux(i_demux[1:0]), .select_demux(select_demux), .d7(d7[1:0]), .d6(d6[1:0]), .d5(d5[1:0]),
    .d4(d4[1:0]), .d3(d3[1:0]), .d2(d2[1:0]), .d1(d1[1:0]), .d0(d0[1:0]));
  DemuxTwoBit demuxtwobit_2 (
    .i_demux(i_demux[3:2]), .select_demux(select_demux), .d7(d7[3:2]), .d6(d6[3:2]), .d5(d5[3:2]),
    .d4(d4[3:2]), .d3(d3[3:2]), .d2(d2[3:2]), .d1(d1[3:2]), .d0(d0[3:2]));
endmodule

module MuxOneBit (
  input  a7,
  input  a6,
  input  a5,
  input  a4,
  input  a3,
  input  a2,
  input  a1,
  input  a0,
  input  [2:0] s2s1s0,
  output F
);

  wire and_1_out, and_2_out, and_3_out, and_4_out, and_5_out, and_6_out, s0_out, s1_out, s2_out, seven_out,
       zero_out;

  not s0 (s0_out, s2s1s0[0]);
  not s1 (s1_out, s2s1s0[1]);
  not s2 (s2_out, s2s1s0[2]);
  and seven (seven_out, a7, s2s1s0[2], s2s1s0[1], s2s1s0[0]);
  and and_1 (and_1_out, a6, s2s1s0[2], s2s1s0[1], s0_out);
  and and_2 (and_2_out, a5, s2s1s0[2], s1_out, s2s1s0[0]);
  and and_3 (and_3_out, a4, s2s1s0[2], s1_out, s0_out);
  and and_4 (and_4_out, a3, s2_out, s2s1s0[1], s2s1s0[0]);
  and and_5 (and_5_out, a2, s2_out, s2s1s0[1], s0_out);
  and and_6 (and_6_out, a1, s2_out, s1_out, s2s1s0[0]);
  and zero (zero_out, a0, s2_out, s1_out, s0_out);
  or or_1 (F, zero_out, and_6_out, and_5_out, and_4_out, and_3_out, and_2_out, and_1_out, seven_out);
endmodule

module MuxTwoBit (
  input  [1:0] k7,
  input  [1:0] k6,
  input  [1:0] k5,
  input  [1:0] k4,
  input  [1:0] k3,
  input  [1:0] k2,
  input  [1:0] k1,
  input  [1:0] k0,
  input  [2:0] select_mux,
  output [1:0] m
);

  MuxOneBit muxonebit_1 (
    .a7(k7[0]), .a6(k6[0]), .a5(k5[0]), .a4(k4[0]), .a3(k3[0]), .a2(k2[0]), .a1(k1[0]), .a0(k0[0]),
    .s2s1s0(select_mux), .F(m[0]));
  MuxOneBit muxonebit_2 (
    .a7(k7[1]), .a6(k6[1]), .a5(k5[1]), .a4(k4[1]), .a3(k3[1]), .a2(k2[1]), .a1(k1[1]), .a0(k0[1]),
    .s2s1s0(select_mux), .F(m[1]));
endmodule

module MuxFourBit (
  input  [3:0] k7,
  input  [3:0] k6,
  input  [3:0] k5,
  input  [3:0] k4,
  input  [3:0] k3,
  input  [3:0] k2,
  input  [3:0] k1,
  input  [3:0] k0,
  input  [2:0] select_mux,
  output [3:0] m
);

  MuxTwoBit muxtwobit_1 (
    .k7(k7[1:0]), .k6(k6[1:0]), .k5(k5[1:0]), .k4(k4[1:0]), .k3(k3[1:0]), .k2(k2[1:0]), .k1(k1[1:0]),
    .k0(k0[1:0]), .select_mux(select_mux), .m(m[1:0]));
  MuxTwoBit muxtwobit_2 (
    .k7(k7[3:2]), .k6(k6[3:2]), .k5(k5[3:2]), .k4(k4[3:2]), .k3(k3[3:2]), .k2(k2[3:2]), .k1(k1[3:2]),
    .k0(k0[3:2]), .select_mux(select_mux), .m(m[3:2]));
endmodule
