// Logisim project sheridan_a5.circ as structural Verilog: 7 circuits, main circuit MemoryTester
module MemoryTester (
  input  [7:0] i,
  input  Clk
);

  wire [7:0] register_1_q, register_8_bit_1_q;

  Register register_1 (.D(i), .clk(Clk), .Q(register_1_q));  // open: en, clr
  Register_8_bit register_8_bit_1 (.i(i), .Clk(Clk), .Q(register_8_bit_1_q));
  Hex_Digit_Display hex_digit_display_1 (.value(register_8_bit_1_q[7:4]));  // open: dp
  Hex_Digit_Display hex_digit_display_2 (.value(register_1_q[7:4]));  // open: dp
  Hex_Digit_Display hex_digit_display_3 (.value(register_1_q[3:0]));  // open: dp
  Hex_Digit_Display hex_digit_display_4 (.value(register_8_bit_1_q[3:0]));  // open: dp
endmodule

module SR_Latch (
  input  S,
  input  R,
  output Q
);

  wire nor_1_out;

  nor nor_1 (nor_1_out, S, Q);
  nor nor_2 (Q, nor_1_out, R);
endmodule

module Level_Sensitive_SR_Latch (
  input  S,
  input  C,
  input  R,
  output Q
);

  wire and_1_out, and_2_out;

  and and_1 (and_1_out, S, C);
  and and_2 (and_2_out, C, R);
  SR_Latch sr_latch_1 (.S(and_1_out), .R(and_2_out), .Q(Q));
endmodule

module D_Latch (
  input  D,
  input  C,
  output Q
);

  wire not_1_out;

  not not_1 (not_1_out, D);
  Level_Sensitive_SR_Latch level_sensitive_sr_latch_1 (.S(D), .C(C), .R(not_1_out), .Q(Q));
endmodule

module D_Flip_Flop (
  input  D,
  input  Clk,
  output Q
);

  wire d_latch_1_q, not_1_out;

  not not_1 (not_1_out, Clk);
  D_Latch d_latch_1 (.D(D), .C(not_1_out), .Q(d_latch_1_q));
  D_Latch d_latch_2 (.D(d_latch_1_q), .C(Clk), .Q(Q));
endmodule

module Register_4_bit (
  input  [3:0] i,
  input  Clk,
  output [3:0] Q
);

  D_Flip_Flop d_flip_flop_1 (.D(i[3]), .Clk(Clk), .Q(Q[3]));
  D_Flip_Flop d_flip_flop_2 (.D(i[2]), .Clk(Clk), .Q(Q[2]));
  D_Flip_Flop d_flip_flop_3 (.D(i[1]), .Clk(Clk), .Q(Q[1]));
  D_Flip_Flop d_flip_flop_4 (.D(i[0]), .Clk(Clk), .Q(Q[0]));
endmodule

module Register_8_bit (
  input  [7:0] i,
  input  Clk,
  output [7:0] Q
);

  Register_4_bit register_4_bit_1 (.i(i[3:0]), .Clk(Clk), .Q(Q[3:0]));
  Register_4_bit register_4_bit_2 (.i(i[7:4]), .Clk(Clk), .Q(Q[7:4]));
endmodule
