// Logisim project sheridan_a6.circ as structural Verilog: 1 circuit, main circuit main
module main (
  input  u,
  input  d,
  input  in_3,
  output H,
  output O,
  output T
);

  wire and_1_out, and_2_out, and_3_out, and_4_out, and_5_out, and_6_out, and_7_out, and_8_out, and_9_out,
       and_10_out, and_11_out, and_12_out, and_13_out, and_14_out, and_16_out, and_17_out, and_18_out;
  wire [1:0] n1_out, register_1_q;

  or n0 (n1_out[1], and_1_out, and_2_out, and_3_out, and_4_out, and_5_out, and_6_out, and_7_out);
  Register #(.width(2)) register_1 (.D(n1_out), .clk(in_3), .Q(register_1_q));  // open: en, clr
  and and_1 (and_1_out, ~u, ~d, register_1_q[1], register_1_q[0]);  // AND_Gate
  and and_2 (and_2_out, ~u, d, register_1_q[1], register_1_q[0]);  // AND_Gate
  and and_3 (and_3_out, u, ~d, register_1_q[1], register_1_q[0]);  // AND_Gate
  and and_4 (and_4_out, ~u, d, ~register_1_q[1], ~register_1_q[0]);  // AND_Gate
  and and_5 (and_5_out, u, d, ~register_1_q[1], register_1_q[0]);  // AND_Gate
  and and_6 (and_6_out, ~u, d, register_1_q[1], ~register_1_q[0]);  // AND_Gate
  and and_7 (and_7_out, u, d, register_1_q[1], ~register_1_q[0]);  // AND_Gate
  and and_8 (and_8_out, ~u, ~d, register_1_q[1], register_1_q[0]);  // AND_Gate
  and and_9 (and_9_out, ~u, d, register_1_q[1], register_1_q[0]);  // AND_Gate
  and and_10 (and_10_out, u, ~d, register_1_q[1], register_1_q[0]);  // AND_Gate
  and and_11 (and_11_out, u, ~d, ~register_1_q[1], ~register_1_q[0]);  // AND_Gate
  and and_12 (and_12_out, u, ~d, ~register_1_q[1], register_1_q[0]);  // AND_Gate
  and and_13 (and_13_out, u, d, ~register_1_q[1], register_1_q[0]);  // AND_Gate
  and and_14 (and_14_out, u, d, register_1_q[1], ~register_1_q[0]);  // AND_Gate
  and and_15 (H, ~register_1_q[1], register_1_q[0]);  // AND_Gate
  and and_16 (and_16_out, ~register_1_q[1], ~register_1_q[0]);  // AND_Gate
  and and_17 (and_17_out, ~register_1_q[1], register_1_q[0]);  // AND_Gate
  and and_18 (and_18_out, register_1_q[1], ~register_1_q[0]);  // AND_Gate
  and and_19 (T, ~register_1_q[1], ~register_1_q[0]);  // AND_Gate
  or n1 (n1_out[0], and_8_out, and_9_out, and_10_out, and_11_out, and_12_out, and_13_out, and_14_out);
  or or_1 (O, and_16_out, and_17_out, and_18_out);
endmodule
