// Logisim project sheridan_a7.circ as structural Verilog: 5 circuits, main circuit MainDataPath
module MainDataPath (
  input  [3:0] input_value
);

  wire Add_out, clk_out, Divide_out, Multiply_out, Next_Num_out, Reset_out, Subtract_out;
  wire [1:0] calcfsm_1_ae_rw_rs_as1_as0;
  wire [3:0] alu_1_result, registerfile_1_regout1, registerfile_1_regout2;
  wire [4:2] calcfsm_1_ae_rw_rs_as1_as0_2;

  Clock clk (.out(clk_out));
  Button Next_Num (.out(Next_Num_out));
  Button Reset (.out(Reset_out));
  Button Add (.out(Add_out));
  Button Subtract (.out(Subtract_out));
  Button Multiply (.out(Multiply_out));
  Button Divide (.out(Divide_out));
  Hex_Digit_Display hex_digit_display_1 (.value(registerfile_1_regout1));  // open: dp
  Hex_Digit_Display hex_digit_display_2 (.value(registerfile_1_regout2));  // open: dp
  Hex_Digit_Display hex_digit_display_3 (.value(alu_1_result));  // open: dp
  ALU alu_1 (
    .ALUen(calcfsm_1_ae_rw_rs_as1_as0_2[4]), .OPsel(calcfsm_1_ae_rw_rs_as1_as0),
    .num1(registerfile_1_regout1), .num2(registerfile_1_regout2), .result(alu_1_result));
  RegisterFile registerfile_1 (
    .RegIn(input_value), .clk(clk_out), .RegWrite(calcfsm_1_ae_rw_rs_as1_as0_2[3]),
    .RegSel(calcfsm_1_ae_rw_rs_as1_as0_2[2]), .RegOut1(registerfile_1_regout1),
    .RegOut2(registerfile_1_regout2));
  CalcFSM calcfsm_1 (
    .a(Add_out), .s(Subtract_out), .m(Multiply_out), .d(Divide_out), .n(Next_Num_out), .r(Reset_out),
    .clk(clk_out), .AE_RW_RS_AS1_AS0({calcfsm_1_ae_rw_rs_as1_as0_2, calcfsm_1_ae_rw_rs_as1_as0}));

  // Notes on the sheet:
  //   num1
  //   OP
  //   num2
  //   =
  //   result
  //   ALU Enable (bit 4)
  //   RegisterWrite (bit 3)
  //   RegisterSelect (bit 2)
  //   ALU Select 1 (bit 1)
  //   ALU Select 0 (bit 0)
endmodule

module CalcFSM (
  input  a,
  input  s,
  input  m,
  input  d,
  input  n,
  input  r,
  input  clk,
  output [4:0] AE_RW_RS_AS1_AS0
);

  wire and_1_out, and_2_out, and_3_out, and_4_out, and_5_out, and_6_out, and_7_out, and_8_out, and_9_out,
       and_10_out, and_11_out, and_12_out, and_13_out, and_14_out, and_15_out, and_16_out, and_17_out,
       and_18_out, and_19_out, and_20_out, and_21_out, and_22_out, and_23_out, and_24_out, and_25_out,
       and_26_out, and_27_out, and_28_out, and_29_out, and_30_out, and_31_out, and_32_out, and_33_out,
       and_34_out, and_35_out, and_36_out, and_37_out, and_38_out, and_39_out, and_40_out, and_41_out,
       and_42_out, and_43_out, and_44_out, and_45_out;
  wire [2:0] n0_out, register_1_q;

  Register #(.width(3)) register_1 (.D(n0_out), .en(1'b1), .clk(clk), .Q(register_1_q));  // open: clr
  and and_1 (and_1_out, n, ~register_1_q[2], ~register_1_q[1], ~register_1_q[0]);  // AND_Gate
  and and_2 (and_2_out, ~n, ~a, ~s, ~m, ~d, ~register_1_q[2], ~register_1_q[1], register_1_q[0]);  // AND_Gate
  and and_3 (and_3_out, n, ~a, ~s, ~m, ~d, ~register_1_q[2], ~register_1_q[1], register_1_q[0]);  // AND_Gate
  and and_4 (and_4_out, ~a, ~s, m, ~d, ~register_1_q[2], ~register_1_q[1], register_1_q[0]);  // AND_Gate
  and and_5 (and_5_out, ~r, register_1_q[2], ~register_1_q[1], register_1_q[0]);  // AND_Gate
  and and_6 (and_6_out, a, ~s, ~m, ~d, ~register_1_q[2], ~register_1_q[1], register_1_q[0]);  // AND_Gate
  and and_7 (and_7_out, ~a, ~s, ~m, d, ~register_1_q[2], ~register_1_q[1], register_1_q[0]);  // AND_Gate
  and and_8 (and_8_out, ~r, ~register_1_q[2], register_1_q[1], ~register_1_q[0]);  // AND_Gate
  and and_9 (and_9_out, ~r, register_1_q[2], register_1_q[1], ~register_1_q[0]);  // AND_Gate
  and and_10 (and_10_out, ~a, s, ~m, ~d, ~register_1_q[2], ~register_1_q[1], register_1_q[0]);  // AND_Gate
  and and_11 (and_11_out, ~a, ~s, m, ~d, ~register_1_q[2], ~register_1_q[1], register_1_q[0]);  // AND_Gate
  and and_12 (and_12_out, ~a, ~s, ~m, d, ~register_1_q[2], ~register_1_q[1], register_1_q[0]);  // AND_Gate
  and and_13 (and_13_out, ~r, register_1_q[2], ~register_1_q[1], ~register_1_q[0]);  // AND_Gate
  and and_14 (and_14_out, ~r, register_1_q[2], ~register_1_q[1], register_1_q[0]);  // AND_Gate
  and and_15 (and_15_out, ~r, register_1_q[2], register_1_q[1], ~register_1_q[0]);  // AND_Gate
  and and_16 (and_16_out, ~n, ~register_1_q[2], ~register_1_q[1], ~register_1_q[0]);  // AND_Gate
  and and_17 (and_17_out, n, ~register_1_q[2], ~register_1_q[1], ~register_1_q[0]);  // AND_Gate
  and and_18 (and_18_out, ~n, ~a, ~s, ~m, ~d, ~register_1_q[2], ~register_1_q[1], register_1_q[0]);  // AND_Gate
  and and_19 (and_19_out, n, ~a, ~s, ~m, ~d, ~register_1_q[2], ~register_1_q[1], register_1_q[0]);  // AND_Gate
  and and_20 (and_20_out, a, ~s, ~m, ~d, ~register_1_q[2], ~register_1_q[1], register_1_q[0]);  // AND_Gate
  and and_21 (and_21_out, ~a, s, ~m, ~d, ~register_1_q[2], ~register_1_q[1], register_1_q[0]);  // AND_Gate
  and and_22 (and_22_out, ~a, ~s, m, ~d, ~register_1_q[2], ~register_1_q[1], register_1_q[0]);  // AND_Gate
  and and_23 (and_23_out, ~a, ~s, ~m, d, ~register_1_q[2], ~register_1_q[1], register_1_q[0]);  // AND_Gate
  and and_24 (and_24_out, ~n, ~a, ~s, ~m, ~d, ~register_1_q[2], ~register_1_q[1], register_1_q[0]);  // AND_Gate
  and and_25 (and_25_out, n, ~a, ~s, ~m, ~d, ~register_1_q[2], ~register_1_q[1], register_1_q[0]);  // AND_Gate
  and and_26 (and_26_out, a, ~s, ~m, ~d, ~register_1_q[2], ~register_1_q[1], register_1_q[0]);  // AND_Gate
  and and_27 (and_27_out, ~a, s, ~m, ~d, ~register_1_q[2], ~register_1_q[1], register_1_q[0]);  // AND_Gate
  and and_28 (and_28_out, ~a, ~s, m, ~d, ~register_1_q[2], ~register_1_q[1], register_1_q[0]);  // AND_Gate
  and and_29 (and_29_out, ~a, ~s, ~m, d, ~register_1_q[2], ~register_1_q[1], register_1_q[0]);  // AND_Gate
  and and_30 (and_30_out, ~r, register_1_q[2], ~register_1_q[1], register_1_q[0]);  // AND_Gate
  and and_31 (and_31_out, r, register_1_q[2], ~register_1_q[1], register_1_q[0]);  // AND_Gate
  and and_32 (and_32_out, ~r, register_1_q[2], register_1_q[1], ~register_1_q[0]);  // AND_Gate
  and and_33 (and_33_out, r, register_1_q[2], register_1_q[1], ~register_1_q[0]);  // AND_Gate
  and and_34 (and_34_out, ~r, register_1_q[2], ~register_1_q[1], ~register_1_q[0]);  // AND_Gate
  and and_35 (and_35_out, r, register_1_q[2], ~register_1_q[1], ~register_1_q[0]);  // AND_Gate
  and and_36 (and_36_out, ~r, register_1_q[2], register_1_q[1], ~register_1_q[0]);  // AND_Gate
  and and_37 (and_37_out, r, register_1_q[2], register_1_q[1], ~register_1_q[0]);  // AND_Gate
  and and_38 (and_38_out, ~r, ~register_1_q[2], register_1_q[1], ~register_1_q[0]);  // AND_Gate
  and and_39 (and_39_out, r, ~register_1_q[2], register_1_q[1], ~register_1_q[0]);  // AND_Gate
  and and_40 (and_40_out, ~r, register_1_q[2], ~register_1_q[1], ~register_1_q[0]);  // AND_Gate
  and and_41 (and_41_out, r, register_1_q[2], ~register_1_q[1], ~register_1_q[0]);  // AND_Gate
  and and_42 (and_42_out, ~r, register_1_q[2], ~register_1_q[1], register_1_q[0]);  // AND_Gate
  and and_43 (and_43_out, r, register_1_q[2], ~register_1_q[1], register_1_q[0]);  // AND_Gate
  and and_44 (and_44_out, ~r, register_1_q[2], register_1_q[1], ~register_1_q[0]);  // AND_Gate
  and and_45 (and_45_out, r, register_1_q[2], register_1_q[1], ~register_1_q[0]);  // AND_Gate
  or AS1 (AE_RW_RS_AS1_AS0[1], and_30_out, and_31_out, and_32_out, and_33_out);
  or AS0 (AE_RW_RS_AS1_AS0[0], and_34_out, and_35_out, and_36_out, and_37_out);
  or AE (AE_RW_RS_AS1_AS0[4], and_38_out, and_39_out, and_40_out, and_41_out, and_42_out, and_43_out, and_44_out, and_45_out);
  or n0 (n0_out[0], and_1_out, and_2_out, and_3_out, and_4_out, and_5_out);
  or n1 (n0_out[1], and_6_out, and_7_out, and_8_out, and_9_out);
  or n2 (n0_out[2], and_10_out, and_11_out, and_12_out, and_13_out, and_14_out, and_15_out);
  or RS (AE_RW_RS_AS1_AS0[2], and_24_out, and_25_out, and_26_out, and_27_out, and_28_out, and_29_out);
  or RW (AE_RW_RS_AS1_AS0[3], and_16_out, and_17_out, and_18_out, and_19_out, and_20_out, and_21_out, and_22_out, and_23_out);
endmodule

module RegisterFile (
  input  [3:0] RegIn,
  input  clk,
  input  RegWrite,
  input  RegSel,
  output [3:0] RegOut1,
  output [3:0] RegOut2
);

  wire and_1_out, and_2_out, undriven;

  Register #(.width(4)) register_1 (.D(RegIn), .en(and_1_out), .clk(clk), .Q(RegOut1), .clr(undriven));
  and and_1 (and_1_out, RegWrite, ~RegSel);  // AND_Gate
  and and_2 (and_2_out, RegWrite, RegSel);
  Register #(.width(4)) register_2 (.D(RegIn), .en(and_2_out), .clk(clk), .Q(RegOut2));  // open: clr
endmodule

module ALU (
  input  ALUen,
  input  [1:0] OPsel,
  input  [3:0] num1,
  input  [3:0] num2,
  output [3:0] result
);

  wire [3:0] cr_adder_1_result, divider_1_out, multiplexer_2_out, multiplier_1_out, subtractor_1_out;

  Multiplexer #(.width(4)) multiplexer_1 (.in0(4'b0000), .in1(multiplexer_2_out), .out(result), .sel(ALUen));
  Subtractor #(.width(4)) subtractor_1 (.a(num1), .b(num2), .out(subtractor_1_out));  // open: bin, bout
  Multiplier #(.width(4)) multiplier_1 (.a(num1), .b(num2), .out(multiplier_1_out));  // open: cin, cout
  Divider #(.width(4)) divider_1 (.a(num1), .b(num2), .out(divider_1_out));  // open: upper, rem
  CR_Adder cr_adder_1 (.num1(num1), .num2(num2), .result(cr_adder_1_result));
  Multiplexer #(.select(2), .width(4)) multiplexer_2 (
    .in0(cr_adder_1_result), .in1(subtractor_1_out), .in2(multiplier_1_out), .in3(divider_1_out),
    .out(multiplexer_2_out), .sel(OPsel));
endmodule

module CR_Adder (
  input  [3:0] num1,
  input  [3:0] num2,
  output [3:0] result
);

  wire adder_1_cout, adder_2_cout, adder_3_cout;

  Adder #(.width(1)) adder_1 (.a(num1[0]), .b(num2[0]), .out(result[0]), .cin(1'b0), .cout(adder_1_cout));
  Adder #(.width(1)) adder_2 (.a(num1[1]), .b(num2[1]), .out(result[1]), .cin(adder_1_cout), .cout(adder_2_cout));
  Adder #(.width(1)) adder_3 (.a(num1[2]), .b(num2[2]), .out(result[2]), .cin(adder_2_cout), .cout(adder_3_cout));
  Adder #(.width(1)) adder_4 (.a(num1[3]), .b(num2[3]), .out(result[3]), .cin(adder_3_cout));  // open: cout

  // Notes on the sheet:
  //   F25B
endmodule
