// Logisim project sheridan_ec.circ as structural Verilog: 1 circuit, main circuit main
module main (
  input  E1,
  input  E2,
  input  E3,
  input  E4,
  input  H1,
  input  H2,
  input  H3,
  input  V,
  input  EW,
  output WinResult
);

  wire and_1_out, and_2_out, and_3_out, and_4_out, EasyAll_out, HardOK_out, not_1_out;

  not not_1 (not_1_out, EW);
  and EasyAll (EasyAll_out, E1, E2, E3, E4);
  and and_1 (and_1_out, ~H1, H2, H3);  // AND_Gate
  and and_2 (and_2_out, H1, ~H2, H3);  // AND_Gate
  and and_3 (and_3_out, H1, H2, ~H3);  // AND_Gate
  and and_4 (and_4_out, H1, H2, H3);
  or HardOK (HardOK_out, and_1_out, and_2_out, and_3_out, and_4_out);
  and Win (WinResult, EasyAll_out, HardOK_out, V, not_1_out);
endmodule
